// Logisim project ini.circ as structural Verilog: 5 circuits, main circuit s1
module s1 (
  input  A,
  input  B,
  input  C,
  output A_B___c
);

  wire A_B_out;

  and A_B (A_B_out, A, B);
  or u_A_B___C (A_B___c, A_B_out, C);

  // Notes on the sheet:
  //   S1
endmodule

module s2 (
  input  A,
  input  B,
  input  C,
  input  D,
  output A_B___C_D
);

  wire A_B_out, C_D_out;

  or A_B (A_B_out, A, B);
  or C_D (C_D_out, C, D);
  and u_A_B___C_D (A_B___C_D, A_B_out, C_D_out, C_D_out);

  // Notes on the sheet:
  //   S2
endmodule

module s3 (
  input  A,
  input  B,
  input  C,
  input  D,
  output out_5
);

  wire A_B_out, nand_1_out, not_1_out;

  and A_B (A_B_out, A, B);
  not not_1 (not_1_out, C);
  nand nand_1 (nand_1_out, C, D);
  or or_1 (out_5, A_B_out, not_1_out, nand_1_out);

  // Notes on the sheet:
  //   S3
endmodule

module s4 (
  input  A,
  input  B,
  input  C,
  input  D,
  output out_5
);

  wire B_C_out, D_B_out, not_1_out, \Ã_B_out ;

  not not_1 (not_1_out, A);
  and \u_Ã_B  (\Ã_B_out , not_1_out, B);
  nand B_C (B_C_out, B, C);
  nor D_B (D_B_out, B, D);
  nand nand_1 (out_5, \Ã_B_out , B_C_out, D_B_out);

  // Notes on the sheet:
  //   S4
endmodule

module s5 (
  input  A,
  input  B,
  input  C,
  input  D,
  output out_5
);

  wire nand_1_out, nand_2_out, not_1_out, not_2_out, not_3_out, or_1_out, or_2_out;

  not not_1 (not_1_out, A);
  not not_2 (not_2_out, B);
  nand nand_1 (nand_1_out, not_1_out, B);
  nand nand_2 (nand_2_out, not_2_out, A);
  not not_3 (not_3_out, C);
  or or_1 (or_1_out, C, D);
  or or_2 (or_2_out, nand_1_out, nand_2_out, not_3_out);
  and and_1 (out_5, or_2_out, or_1_out);

  // Notes on the sheet:
  //   S5
endmodule
