// Logisim project lab22.circ as structural Verilog: 1 circuit, main circuit main
module main (
  input  a,
  input  b,
  input  c,
  input  d,
  output out_5
);

  wire and_1_out, and_2_out, and_3_out, not_1_out, not_2_out, not_3_out;

  not not_1 (not_1_out, b);
  not not_2 (not_2_out, c);
  not not_3 (not_3_out, a);
  and and_1 (and_1_out, a, b, not_2_out);
  and and_2 (and_2_out, a, not_1_out, c);
  and and_3 (and_3_out, not_3_out, not_2_out, d);
  or or_1 (out_5, and_3_out, and_1_out, and_2_out);
endmodule
