// Logisim project lab3.circ as structural Verilog: 2 circuits, main circuit main
module main (
  input  A,
  input  B,
  input  C,
  output D0,
  output D1,
  output D2,
  output D3,
  output D5,
  output D6,
  output D7,
  output D7_2
);

  wire not_1_out, not_2_out, not_3_out;

  not not_1 (not_1_out, A);
  not not_2 (not_2_out, B);
  not not_3 (not_3_out, C);
  and and_1 (D0, not_1_out, not_2_out, not_3_out);
  and and_2 (D1, not_1_out, not_2_out, C);
  and and_3 (D2, not_1_out, B, not_3_out);
  and and_4 (D3, not_1_out, B, C);
  and and_5 (D5, A, not_2_out, not_3_out);
  and and_6 (D6, A, not_2_out, C);
  and and_7 (D7, A, B, not_3_out);
  and and_8 (D7_2, A, B, C);
endmodule

module tes (
  input  A0,
  input  B0,
  input  A1,
  input  B1,
  input  A2,
  input  B2,
  input  A3,
  input  B3,
  output Saida
);

  wire xor_1_out, xor_2_out, xor_3_out, xor_4_out;

  xor xor_1 (xor_1_out, A0, B0);
  xor xor_2 (xor_2_out, A1, B1);
  xor xor_3 (xor_3_out, A2, B2);
  xor xor_4 (xor_4_out, A3, B3);
  nor nor_1 (Saida, xor_1_out, xor_2_out, xor_3_out, xor_4_out);
endmodule
