// Logisim project a2.circ as structural Verilog: 1 circuit, main circuit main
module main (
  input  B,
  input  A,
  input  C,
  input  D,
  output out_5
);

  wire and_1_out, and_2_out, and_3_out, and_4_out, nor_1_out, not_1_out;

  not not_1 (not_1_out, B);
  and and_1 (and_1_out, A, C);
  and and_2 (and_2_out, C, D);
  and and_3 (and_3_out, not_1_out, and_1_out);
  nor nor_1 (nor_1_out, A, and_2_out);
  and and_4 (and_4_out, not_1_out, nor_1_out);
  or or_1 (out_5, and_3_out, and_4_out);

  // Notes on the sheet:
  //   C.D
  //   A.C
  //   ~B. A.C
  //   A+C.D
  //   ~(A+C.D)
  //   ~B. ~(A+C.D)
  //   ~B.A.C + ~B . Ã.~C + ~B.Ã.~D
endmodule
